# Fritzing sketch Project-sketch (saved by Fritzing 0.9.4)
breadboards: 1

parts:
  Arduino_Nano = Arduino Nano (Rev3.0) (ICSP)
  LED1 = LED - 3mm [color="Red (633nm)" package="3 mm [THT]"]
  LED2 = LED - 3mm [color="Yellow (595nm)" package="3 mm [THT]"]
  LED3 = LED - 3mm [color="Green (565nm)" package="3 mm [THT]"]
  R1 = Resistor [tolerance=±5% resistance=1k package="2512 [SMD]"]
  R2 = Resistor [tolerance=±5% resistance=1k package="2512 [SMD]"]
  R3 = Resistor [tolerance=±5% resistance=1k package="2512 [SMD]"]
  OLED = Grove OLED 128x96
  A1 = Piezo Speaker
  S1 = HC-SR04 Ultrasonic Distance Sensor
  R4 = Resistor [tolerance=±5% resistance=1k package="2512 [SMD]"]
  T = TRANSISTOR_NPN [package=to-92-ammo]

nets:
  GND: Arduino_Nano.GND, R1.Pin_0, R2.Pin_0, R3.Pin_0, OLED.GND, S1.GND, T.C
  N1: Arduino_Nano.D3, S1.ECHO
  N2: Arduino_Nano.D4, S1.TRIG
  N3: Arduino_Nano.D5, R4.Pin_0
  N4: Arduino_Nano.D6, LED1.anode
  N5: Arduino_Nano.D7, LED2.anode
  N6: Arduino_Nano.D8, LED3.anode
  VCC: Arduino_Nano.5V, OLED.VCC, A1.pin1, S1.VCC
  N7: Arduino_Nano.A5, OLED.SCL
  N8: Arduino_Nano.A4, OLED.SDA
  N9: LED1.cathode, R1.Pin_1
  N10: LED2.cathode, R2.Pin_1
  N11: LED3.cathode, R3.Pin_1
  N12: A1.pin2, T.E
  N13: R4.Pin_1, T.B
