# Fritzing sketch Project-sketch_new (saved by Fritzing 0.9.4)
breadboards: 1

parts:
  Arduino_Nano = Arduino Nano (Rev3.0) (ICSP)
  LED1 = LED - 3mm [color="Red (633nm)" package="3 mm [THT]"]
  LED2 = LED - 3mm [color="Yellow (595nm)" package="3 mm [THT]"]
  R1 = Resistor [tolerance=±5% resistance=1k package="2512 [SMD]"]
  R2 = Resistor [tolerance=±5% resistance=1k package="2512 [SMD]"]
  R3 = Resistor [tolerance=±5% resistance=1k package="2512 [SMD]"]
  OLED = Grove OLED 128x96
  Piezo_Buzzer = Piezo Speaker
  Sensor = HC-SR04 Ultrasonic Distance Sensor
  LED3 = LED - 3mm [color="Green (565nm)" package="3 mm [THT]"]

nets:
  GND: Arduino_Nano.GND, R1.Pin_0, R2.Pin_0, R3.Pin_0, OLED.GND, Piezo_Buzzer.pin1, Sensor.GND
  N1: Arduino_Nano.D3, LED3.anode
  N2: Arduino_Nano.D4, LED2.anode
  N3: Arduino_Nano.D5, LED1.cathode, LED1.anode, R1.Pin_1
  N4: Arduino_Nano.D8, Piezo_Buzzer.pin2
  N5: Arduino_Nano.D9, Sensor.TRIG
  N6: Arduino_Nano.D10, Sensor.ECHO
  VCC: Arduino_Nano.5V, OLED.VCC, Sensor.VCC
  N7: Arduino_Nano.A5, OLED.SCL
  N8: Arduino_Nano.A4, OLED.SDA
  N9: LED2.cathode, R2.Pin_1
  N10: R3.Pin_1, LED3.cathode
