# Fritzing sketch uas-sketch (saved by Fritzing 0.9.4)
breadboards: 1

parts:
  Arduino_Nano = Arduino Nano (Rev3.0) (ICSP)
  S1 = Pushbutton [package="[THT]"]
  S2 = Pushbutton [package="[THT]"]
  S3 = Pushbutton [package="[THT]"]
  S4 = Pushbutton [package="[THT]"]
  Potensio = POT [package=pot_mammoth]

nets:
  N1: Arduino_Nano.GND, S1.Pin_3, S1.Pin_4, S2.Pin_3, S2.Pin_4, S3.Pin_3, S3.Pin_4, S4.Pin_3, S4.Pin_4, Potensio.E
  N2: Arduino_Nano.D2, S4.Pin_1, S4.Pin_2
  N3: Arduino_Nano.D3, S3.Pin_1, S3.Pin_2
  N4: Arduino_Nano.D4, S2.Pin_1, S2.Pin_2
  N5: Arduino_Nano.D5, S1.Pin_1, S1.Pin_2
  N6: Arduino_Nano.D8, Arduino_Nano.D11/MOSI
  N7: Arduino_Nano.A0, Potensio.A
